// Logisim project halfAdder.circ as structural Verilog
module half_Adder (
  input  a,
  input  b,
  output Carry,
  output Out
);

  and and_1 (Carry, a, b);
  xor xor_1 (Out, a, b);
endmodule

module Full_Adder (
  input  Carry_in,
  input  a_in,
  input  b_in,
  output Result,
  output Carry
);

  wire half_adder_1_carry, half_adder_1_out, half_adder_2_carry;

  half_Adder half_adder_1 (.a(a_in), .b(b_in), .Carry(half_adder_1_carry), .Out(half_adder_1_out));
  half_Adder half_adder_2 (.a(Carry_in), .b(half_adder_1_out), .Carry(half_adder_2_carry), .Out(Result));
  or or_1 (Carry, half_adder_2_carry, half_adder_1_carry);
endmodule

module Adder_8_bits (
  input  a0,
  input  a1,
  input  a2,
  input  a3,
  input  a4,
  input  a5,
  input  a6,
  input  a7,
  input  b0,
  input  b1,
  input  b2,
  input  b3,
  input  b4,
  input  b5,
  input  b6,
  input  b7,
  output r0,
  output r1,
  output r2,
  output r3,
  output r4,
  output r5,
  output r6,
  output r7,
  output Overflow
);

  wire full_adder_1_carry, full_adder_2_carry, full_adder_3_carry, full_adder_4_carry, full_adder_5_carry,
       full_adder_6_carry, full_adder_7_carry;

  Full_Adder full_adder_1 (.Carry_in(1'b0), .a_in(a0), .b_in(b0), .Result(r0), .Carry(full_adder_1_carry));
  Full_Adder full_adder_2 (
    .Carry_in(full_adder_1_carry), .a_in(a1), .b_in(b1), .Result(r1), .Carry(full_adder_2_carry));
  Full_Adder full_adder_3 (
    .Carry_in(full_adder_2_carry), .a_in(a2), .b_in(b2), .Result(r2), .Carry(full_adder_3_carry));
  Full_Adder full_adder_4 (
    .Carry_in(full_adder_3_carry), .a_in(a3), .b_in(b3), .Result(r3), .Carry(full_adder_4_carry));
  Full_Adder full_adder_5 (
    .Carry_in(full_adder_4_carry), .a_in(a4), .b_in(b4), .Result(r4), .Carry(full_adder_5_carry));
  Full_Adder full_adder_6 (
    .Carry_in(full_adder_5_carry), .a_in(a5), .b_in(b5), .Result(r5), .Carry(full_adder_6_carry));
  Full_Adder full_adder_7 (
    .Carry_in(full_adder_6_carry), .a_in(a6), .b_in(b6), .Result(r6), .Carry(full_adder_7_carry));
  Full_Adder full_adder_8 (.Carry_in(full_adder_7_carry), .a_in(a7), .b_in(b7), .Result(r7), .Carry(Overflow));

  // Notes on the sheet:
  //   Const 0
endmodule

module Two_s_complement (
  input  in_1,
  input  in_2,
  input  in_3,
  input  in_4,
  input  in_5,
  input  in_6,
  input  in_7,
  input  in_8,
  output out_9,
  output out_10,
  output out_11,
  output out_12,
  output out_13,
  output out_14,
  output out_15,
  output out_16,
  output out_17
);

  wire not_1_out, not_2_out, not_3_out, not_4_out, not_5_out, not_6_out, not_7_out, not_8_out;

  not not_1 (not_1_out, in_1);
  not not_2 (not_2_out, in_2);
  not not_3 (not_3_out, in_3);
  not not_4 (not_4_out, in_4);
  not not_5 (not_5_out, in_5);
  not not_6 (not_6_out, in_6);
  not not_7 (not_7_out, in_7);
  not not_8 (not_8_out, in_8);
  Adder_8_bits adder_8_bits_1 (
    .r0(out_9), .r1(out_10), .r2(out_11), .r3(out_12), .r4(out_13), .r5(out_14), .r6(out_15), .r7(out_16),
    .Overflow(out_17), .b0(1'b1), .b1(1'b0), .b2(1'b0), .b3(1'b0), .b4(1'b0), .b5(1'b0), .b6(1'b0),
    .b7(1'b0), .a0(not_1_out), .a1(not_2_out), .a2(not_3_out), .a3(not_4_out), .a4(not_5_out),
    .a5(not_6_out), .a6(not_7_out), .a7(not_8_out));
endmodule

module Subtraction (
  input  a0,
  input  a1,
  input  a2,
  input  a3,
  input  a4,
  input  a5,
  input  a6,
  input  a7,
  input  b0,
  input  b1,
  input  b2,
  input  b3,
  input  b4,
  input  b5,
  input  b6,
  input  b7,
  output r0,
  output r1,
  output r2,
  output r3,
  output r4,
  output r5,
  output r6,
  output r7,
  output Overflow
);

  wire full_adder_1_carry, full_adder_2_carry, full_adder_3_carry, full_adder_4_carry, full_adder_5_carry,
       full_adder_6_carry, full_adder_7_carry, two_s_complement_1_out_9, two_s_complement_1_out_10,
       two_s_complement_1_out_11, two_s_complement_1_out_12, two_s_complement_1_out_13,
       two_s_complement_1_out_14, two_s_complement_1_out_15, two_s_complement_1_out_16;

  Two_s_complement two_s_complement_1 (
    .in_1(b0), .in_2(b1), .in_3(b2), .in_4(b3), .in_5(b4), .in_6(b5), .in_7(b6), .in_8(b7),
    .out_9(two_s_complement_1_out_9), .out_10(two_s_complement_1_out_10), .out_11(two_s_complement_1_out_11),
    .out_12(two_s_complement_1_out_12), .out_13(two_s_complement_1_out_13),
    .out_14(two_s_complement_1_out_14), .out_15(two_s_complement_1_out_15), .out_16(two_s_complement_1_out_16));  // open: out_17
  Full_Adder full_adder_1 (
    .Carry_in(1'b0), .a_in(a0), .b_in(two_s_complement_1_out_9), .Result(r0), .Carry(full_adder_1_carry));
  Full_Adder full_adder_2 (
    .Carry_in(full_adder_1_carry), .a_in(a1), .b_in(two_s_complement_1_out_10), .Result(r1),
    .Carry(full_adder_2_carry));
  Full_Adder full_adder_3 (
    .Carry_in(full_adder_2_carry), .a_in(a2), .b_in(two_s_complement_1_out_11), .Result(r2),
    .Carry(full_adder_3_carry));
  Full_Adder full_adder_4 (
    .Carry_in(full_adder_3_carry), .a_in(a3), .b_in(two_s_complement_1_out_12), .Result(r3),
    .Carry(full_adder_4_carry));
  Full_Adder full_adder_5 (
    .Carry_in(full_adder_4_carry), .a_in(a4), .b_in(two_s_complement_1_out_13), .Result(r4),
    .Carry(full_adder_5_carry));
  Full_Adder full_adder_6 (
    .Carry_in(full_adder_5_carry), .a_in(a5), .b_in(two_s_complement_1_out_14), .Result(r5),
    .Carry(full_adder_6_carry));
  Full_Adder full_adder_7 (
    .Carry_in(full_adder_6_carry), .a_in(a6), .b_in(two_s_complement_1_out_15), .Result(r6),
    .Carry(full_adder_7_carry));
  Full_Adder full_adder_8 (
    .Carry_in(full_adder_7_carry), .a_in(a7), .b_in(two_s_complement_1_out_16), .Result(r7), .Carry(Overflow));

  // Notes on the sheet:
  //   Const 0
endmodule

module Quarter_Multiplier (
  input  [7:0] in_1,
  input  in_2,
  output [7:0] out_3,
  output [7:0] out_4
);

  Shifter shifter_1 (.in(in_1), .\dist (3'b001), .out(out_3));
  and and_1 (out_4[0], in_2, in_1[0]);
  and and_2 (out_4[1], in_2, in_1[1]);
  and and_3 (out_4[2], in_2, in_1[2]);
  and and_4 (out_4[3], in_2, in_1[3]);
  and and_5 (out_4[4], in_2, in_1[4]);
  and and_6 (out_4[5], in_2, in_1[5]);
  and and_7 (out_4[6], in_2, in_1[6]);
  and and_8 (out_4[7], in_2, in_1[7]);
endmodule

module Full_Multiplier (
  input  a0,
  input  a1,
  input  a2,
  input  a3,
  input  a4,
  input  a5,
  input  a6,
  input  a7,
  input  b0,
  input  b1,
  input  b2,
  input  b3,
  input  b4,
  input  b5,
  input  b6,
  input  b7,
  output r0,
  output r1,
  output r2,
  output r3,
  output r4,
  output r5,
  output r6,
  output r7
);

  wire [7:0] adder_8_bits_1_r0, adder_8_bits_2_r0, quarter_multiplier_1_out_3, quarter_multiplier_1_out_4,
       quarter_multiplier_2_out_3, quarter_multiplier_2_out_4, quarter_multiplier_3_out_3,
       quarter_multiplier_3_out_4, quarter_multiplier_4_out_4;

  Quarter_Multiplier quarter_multiplier_1 (
    .in_1({b7, b6, b5, b4, b3, b2, b1, b0}), .in_2(a0), .out_3(quarter_multiplier_1_out_3),
    .out_4(quarter_multiplier_1_out_4));
  Quarter_Multiplier quarter_multiplier_2 (
    .in_1(quarter_multiplier_1_out_3), .in_2(a1), .out_3(quarter_multiplier_2_out_3),
    .out_4(quarter_multiplier_2_out_4));
  Adder_8_bits adder_8_bits_1 (
    .r0(adder_8_bits_1_r0[0]), .r1(adder_8_bits_1_r0[1]), .r2(adder_8_bits_1_r0[2]),
    .r3(adder_8_bits_1_r0[3]), .r4(adder_8_bits_1_r0[4]), .r5(adder_8_bits_1_r0[5]),
    .r6(adder_8_bits_1_r0[6]), .r7(adder_8_bits_1_r0[7]), .b0(quarter_multiplier_2_out_4[0]),
    .b1(quarter_multiplier_2_out_4[1]), .b2(quarter_multiplier_2_out_4[2]),
    .b3(quarter_multiplier_2_out_4[3]), .b4(quarter_multiplier_2_out_4[4]),
    .b5(quarter_multiplier_2_out_4[5]), .b6(quarter_multiplier_2_out_4[6]),
    .b7(quarter_multiplier_2_out_4[7]), .a0(quarter_multiplier_1_out_4[0]),
    .a1(quarter_multiplier_1_out_4[1]), .a2(quarter_multiplier_1_out_4[2]),
    .a3(quarter_multiplier_1_out_4[3]), .a4(quarter_multiplier_1_out_4[4]),
    .a5(quarter_multiplier_1_out_4[5]), .a6(quarter_multiplier_1_out_4[6]), .a7(quarter_multiplier_1_out_4[7]));  // open: Overflow
  Quarter_Multiplier quarter_multiplier_3 (
    .in_1(quarter_multiplier_2_out_3), .in_2(a2), .out_3(quarter_multiplier_3_out_3),
    .out_4(quarter_multiplier_3_out_4));
  Quarter_Multiplier quarter_multiplier_4 (
    .in_1(quarter_multiplier_3_out_3), .in_2(a3), .out_4(quarter_multiplier_4_out_4));  // open: out_3
  Adder_8_bits adder_8_bits_2 (
    .r0(adder_8_bits_2_r0[0]), .r1(adder_8_bits_2_r0[1]), .r2(adder_8_bits_2_r0[2]),
    .r3(adder_8_bits_2_r0[3]), .r4(adder_8_bits_2_r0[4]), .r5(adder_8_bits_2_r0[5]),
    .r6(adder_8_bits_2_r0[6]), .r7(adder_8_bits_2_r0[7]), .b0(quarter_multiplier_3_out_4[0]),
    .b1(quarter_multiplier_3_out_4[1]), .b2(quarter_multiplier_3_out_4[2]),
    .b3(quarter_multiplier_3_out_4[3]), .b4(quarter_multiplier_3_out_4[4]),
    .b5(quarter_multiplier_3_out_4[5]), .b6(quarter_multiplier_3_out_4[6]),
    .b7(quarter_multiplier_3_out_4[7]), .a0(adder_8_bits_1_r0[0]), .a1(adder_8_bits_1_r0[1]),
    .a2(adder_8_bits_1_r0[2]), .a3(adder_8_bits_1_r0[3]), .a4(adder_8_bits_1_r0[4]),
    .a5(adder_8_bits_1_r0[5]), .a6(adder_8_bits_1_r0[6]), .a7(adder_8_bits_1_r0[7]));  // open: Overflow
  Adder_8_bits adder_8_bits_3 (
    .r0(r0), .r1(r1), .r2(r2), .r3(r3), .r4(r4), .r5(r5), .r6(r6), .r7(r7),
    .b0(quarter_multiplier_4_out_4[0]), .b1(quarter_multiplier_4_out_4[1]),
    .b2(quarter_multiplier_4_out_4[2]), .b3(quarter_multiplier_4_out_4[3]),
    .b4(quarter_multiplier_4_out_4[4]), .b5(quarter_multiplier_4_out_4[5]),
    .b6(quarter_multiplier_4_out_4[6]), .b7(quarter_multiplier_4_out_4[7]), .a0(adder_8_bits_2_r0[0]),
    .a1(adder_8_bits_2_r0[1]), .a2(adder_8_bits_2_r0[2]), .a3(adder_8_bits_2_r0[3]),
    .a4(adder_8_bits_2_r0[4]), .a5(adder_8_bits_2_r0[5]), .a6(adder_8_bits_2_r0[6]), .a7(adder_8_bits_2_r0[7]));  // open: Overflow
endmodule
